# Fritzing sketch follow_the_light (saved by Fritzing 0.9.3b)
breadboards: 1

parts:
  Componente1 = Arduino Uno (Rev3)
  R1 = Rotary Potentiometer (Small) [maximum_resistance=100kΩ package=THT]
  LED1 = LED - 5mm [color="Red (633nm)" package="5 mm [THT]"]
  R2 = Resistor [tolerance=±5% resistance=220 package=THT]
  LED2 = LED - 5mm [color="Green (555nm)" package="5 mm [THT]"]
  R3 = Resistor [tolerance=±5% resistance=220 package=THT]
  S1 = Pushbutton [package="[THT]"]
  R4 = Resistor [tolerance=±5% resistance=10k package=THT]
  LED3 = LED - 5mm [color="Green (555nm)" package="5 mm [THT]"]
  S2 = Pushbutton [package="[THT]"]
  R5 = Resistor [tolerance=±5% resistance=220 package=THT]
  R6 = Resistor [tolerance=±5% resistance=10k package=THT]
  LED4 = LED - 5mm [color="Green (555nm)" package="5 mm [THT]"]
  S3 = Pushbutton [package="[THT]"]
  R7 = Resistor [tolerance=±5% resistance=10k package=THT]
  R8 = Resistor [tolerance=±5% resistance=220 package=THT]

nets:
  N1: Componente1.A3, R1.wiper
  N2: Componente1.D11_PWM/MOSI, LED3.cathode, S2.Pin_1, S2.Pin_2, R6.Pin_0
  N3: Componente1.D12/MISO, LED4.cathode, S3.Pin_1, S3.Pin_2, R7.Pin_0
  N4: Componente1.D2, LED2.cathode, S1.Pin_1, S1.Pin_2, R4.Pin_0
  N5: Componente1.D3_PWM, R3.Pin_1
  N6: Componente1.D4, R5.Pin_1
  N7: Componente1.D5_PWM, R8.Pin_1
  N8: Componente1.D6_PWM, R2.Pin_1
  N9: Componente1.5V, R1.leg1, S1.Pin_3, S1.Pin_4, S2.Pin_3, S2.Pin_4, S3.Pin_3, S3.Pin_4
  N10: Componente1.GND, R1.leg2, LED1.cathode, R4.Pin_1, R6.Pin_1, R7.Pin_1
  N11: LED1.anode, R2.Pin_0
  N12: LED2.anode, R3.Pin_0
  N13: LED3.anode, R5.Pin_0
  N14: LED4.anode, R8.Pin_0
