# Fritzing sketch consegna04 (saved by Fritzing 0.9.3b)
breadboards: 1

parts:
  Componente1 = Arduino Uno (Rev3)
  Raspberry_Pi_1 = Raspberry Pi 3 [part_number=RPI-3-V1.2]
  L_FAILED_ACCESS = LED - 5mm [color="Red (633nm)" package="5 mm [THT]"]
  L_INSIDE = LED - 5mm [color="Green (555nm)" package="5 mm [THT]"]
  R1 = Resistor [tolerance=±5% resistance=220 package=THT]
  R2 = Resistor [tolerance=±5% resistance=220 package=THT]
  BT_EXIT = Pushbutton [package="[THT]"]
  R3 = Resistor [tolerance=±2% resistance=10k package=THT]
  L_VALUE = LED - 5mm [color="Red (633nm)" package="5 mm [THT]"]
  LED1 = LED - 5mm [color="Green (555nm)" package="5 mm [THT]"]
  R4 = Resistor [tolerance=±5% resistance=220 package=THT]
  R5 = Resistor [tolerance=±5% resistance=220 package=THT]
  J2 = Basic Servo
  Componente2 = Bluetooth HC-05 Macho
  U1 = TMP36 [package=to-92-kit]  # not connected
  PIR1 = PIR sensor
  hc-sr1 = hc-sr04

nets:
  N1: Componente1.D8, hc-sr1.Trig
  N2: Componente1.D9_PWM, J2.pulse
  N3: Componente1.D11_PWM/MOSI, R5.Pin_1
  N4: Componente1.D12/MISO, BT_EXIT.Pin_3, BT_EXIT.Pin_4, R3.Pin_1
  N5: Componente1.D13/SCK, R4.Pin_1
  N6: Componente1.D3_PWM, Componente2.RXD
  N7: Componente1.D4, Componente2.TXD
  N8: Componente1.D6_PWM, PIR1.SIG
  N9: Componente1.D7, hc-sr1.Echo
  VCC: Componente1.5V, BT_EXIT.Pin_1, BT_EXIT.Pin_2, J2.vcc, Componente2.VCC, PIR1.VDD, hc-sr1.VCC
  GND: Componente1.GND, R3.Pin_0, L_VALUE.cathode, LED1.cathode, J2.gnd, Componente2.GND, PIR1.GND, hc-sr1.GND
  N10: Raspberry_Pi_1.GND, L_FAILED_ACCESS.cathode, L_INSIDE.cathode
  N11: Raspberry_Pi_1.GPIO24, R2.Pin_1
  N12: Raspberry_Pi_1.GPIO23, R1.Pin_1
  N13: L_FAILED_ACCESS.anode, R2.Pin_0
  N14: L_INSIDE.anode, R1.Pin_0
  N15: L_VALUE.anode, R5.Pin_0
  N16: LED1.anode, R4.Pin_0
